# Fritzing sketch SchemaElectrique (saved by Fritzing 0.9.3b)

parts:
  Composant1 = Arduino Nano (Rev3.0)
  GY1 = MPU-6050 Board GY-521 [form="♀ (female)" package=THT]
  M2 = ESC
  920KV_Motor2 = DJI 920 KV Motor  # not connected
  M3 = ESC
  920KV_Motor3 = DJI 920 KV Motor  # not connected
  M4 = ESC
  920KV_Motor4 = DJI 920 KV Motor  # not connected
  M5 = ESC
  920KV_Motor5 = DJI 920 KV Motor  # not connected
  U1 = LIPO-2000mAh [package=lipo-2000]  # not connected
  R1 = Trimmer Potentiometer [maximum_resistance=10kΩ package=THT]

nets:
  N1: Composant1.D4, M2.DATA
  N2: Composant1.D5, M3.DATA
  N3: Composant1.D6, M4.DATA
  N4: Composant1.D7, M5.DATA
  N5: Composant1.GND, GY1.pin2, R1.leg2
  5V: Composant1.5V, GY1.pin1, M2.5V, R1.leg1
  N6: Composant1.A5, GY1.pin3
  N7: Composant1.A4, GY1.pin4
  N8: Composant1.A0, R1.wiper
  GND: M2.GND, M3.GND, M4.GND

custom parts:
  MPU-6050 Board GY-521: Acelerometro y Giroscopio MPU-6050 Board GY-521
  DJI 920 KV Motor: DJI Brushless Outrunner 2212/920K Motor F330-550
